# Fritzing sketch schorlephasediagram (saved by Fritzing 0.9.3b)
breadboards: 1

parts:
  R1 = Resistor [tolerance=±5% resistance=10k package=THT]
  PCB1 = Arduino Shield PCB  # not connected
  Arduino1 = Arduino Uno (Rev3)
  BUTTON1 = Arcade Button (blue)
  LED1 = RGB LED - (4 legs) [package="5 mm [THT]"]
  SP1 = SPEAKER [package=pcb_mount_speaker]
  Part4 = Adafruit DRV8833 DC/Stepper Motor Driver [part_number="Adafruit #3297"]
  M1 = Stepper Motor - Unipolar
  Part7 = Audio FX Sound Board + 2x2W Amp

nets:
  N1: R1.Pin_0, Arduino1.D2, BUTTON1.no_name_yet#2
  GND: R1.Pin_1, Arduino1.GND, LED1.green_cathode, Part4.GND, Part7.GND
  N2: Arduino1.D8, Part4.AIN2
  N3: Arduino1.D9_PWM, Part4.BIN2
  N4: Arduino1.D10_PWM/SS, Part4.BIN1
  N5: Arduino1.D3_PWM, Part7.1
  N6: Arduino1.D4, Part7.0
  N7: Arduino1.D5_PWM, Part7.2
  N8: Arduino1.D6_PWM, LED1.red_cathode
  N9: Arduino1.D7, Part4.AIN1
  5V: Arduino1.5V, BUTTON1.no_name_yet#1, LED1.common_anode, Part4.!SLEEP, Part7.VIN
  N10: Arduino1.VIN, Part4.VMOTOR
  N11: SP1.+, Part7.R-
  N12: SP1.-, Part7.R+
  N13: Part4.AOUT2, M1.COMMON_2
  N14: Part4.AOUT1, M1.D
  N15: Part4.BOUT1, M1.C
  N16: Part4.BOUT2, M1.B

custom parts:
  Arduino Shield PCB: Plain PCB Shaped to fit an Arduino "Shield"
  Arcade Button (blue): Adafruit Arcade Button (blue)
  Adafruit DRV8833 DC/Stepper Motor Driver: Spin two DC motors or step one bi-polar or uni-polar stepper with up to 1.2A per channel using the DRV8833. This motor driver chip is a nice alternative to the TB6612 driver. Like that chip, you get 2 full H-bridges, but this chip is better for low voltage uses (can run from 2.7V up to 10.8V motor power) and has built in current limiting capability. We set it up for 1A current limiting so you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
  Audio FX Sound Board + 2x2W Amp: The Adafruit Sound Board, the fastest way to add audio effects to a project!

// code stored in the sketch: Button.ino
/*
  Button
 
 Turns on and off a light emitting diode(LED) connected to digital  
 pin 13, when pressing a pushbutton attached to pin 2. 
 
 
 The circuit:
 * LED attached from pin 13 to ground 
 * pushbutton attached to pin 2 from +5V
 * 10K resistor attached to pin 2 from ground
 
 * Note: on most Arduinos there is already an LED on the board
 attached to pin 13.
 
 
 created 2005
 by DojoDave <http://www.0j0.org>
 modified 30 Aug 2011
 by Tom Igoe
 
 This example code is in the public domain.
 
 http://www.arduino.cc/en/Tutorial/Button
 */

// constants won't change. They're used here to 
// set pin numbers:
const int buttonPin = 2;     // the number of the pushbutton pin
const int ledPin =  13;      // the number of the LED pin

// variables will change:
int buttonState = 0;         // variable for reading the pushbutton status

void setup() {
  // initialize the LED pin as an output:
  pinMode(ledPin, OUTPUT);      
  // initialize the pushbutton pin as an input:
  pinMode(buttonPin, INPUT);     
}

void loop(){
  // read the state of the pushbutton value:
  buttonState = digitalRead(buttonPin);

  // check if the pushbutton is pressed.
  // if it is, the buttonState is HIGH:
  if (buttonState == HIGH) {     
    // turn LED on:    
    digitalWrite(ledPin, HIGH);  
  } 
  else {
    // turn LED off:
    digitalWrite(ledPin, LOW); 
  }
}
